# Fritzing sketch memory-game (saved by Fritzing 0.9.3b)
breadboards: 1

parts:
  Arduino1 = Arduino Mini (Rev5)
  LED1 = LED - 5mm [color="Red (633nm)" package="5 mm [THT]"]
  R1 = Resistor [tolerance=±5% resistance=4.7k package="0603 [SMD]"]
  S1 = Pushbutton [package="[THT]"]
  R2 = Resistor [tolerance=±5% resistance=220k package="0603 [SMD]"]
  LED2 = LED - 5mm [color="Blue (470nm)" package="5 mm [THT]"]
  R3 = Resistor [tolerance=±5% resistance=4.7k package="0603 [SMD]"]
  S2 = Pushbutton [package="[THT]"]
  R4 = Resistor [tolerance=±5% resistance=220 package="0603 [SMD]"]
  LED3 = LED - 5mm [color="Yellow (595nm)" package="5 mm [THT]"]
  S3 = Pushbutton [package="[THT]"]
  R5 = Resistor [tolerance=±5% resistance=220 package="0603 [SMD]"]
  R6 = Resistor [tolerance=±5% resistance=4.7k package="0603 [SMD]"]
  LED4 = LED - 5mm [color="Green (555nm)" package="5 mm [THT]"]
  S4 = Pushbutton [package="[THT]"]
  R7 = Resistor [tolerance=±5% resistance=220 package="0603 [SMD]"]
  R8 = Resistor [tolerance=±5% resistance=4.7k package="0603 [SMD]"]
  J1 = Piezo Speaker
  VCC1 = 4 x AAA Battery Mount

nets:
  N1: Arduino1.GND, R1.Pin_1, R2.Pin_1, R3.Pin_1, R4.Pin_1, R5.Pin_1, R6.Pin_1, R7.Pin_1, R8.Pin_1, J1.pin1, VCC1.-
  N2: Arduino1.D2, S2.Pin_1, S2.Pin_2, R4.Pin_0
  N3: Arduino1.D3_PWM, S3.Pin_1, S3.Pin_2, R5.Pin_0
  N4: Arduino1.D4, S4.Pin_1, S4.Pin_2, R7.Pin_0
  N5: Arduino1.D5_PWM, S1.Pin_1, S1.Pin_2, R2.Pin_0
  N6: Arduino1.D7, LED2.cathode
  N7: Arduino1.D8, LED3.cathode
  N8: Arduino1.D9_PWM, LED4.cathode
  N9: Arduino1.5V, S1.Pin_3, S1.Pin_4, S2.Pin_3, S2.Pin_4, S3.Pin_3, S3.Pin_4, S4.Pin_3, S4.Pin_4, VCC1.+
  N10: Arduino1.D12, J1.pin2
  N11: Arduino1.D10_PWM, LED1.cathode
  N12: LED1.anode, R1.Pin_0
  N13: LED2.anode, R3.Pin_0
  N14: LED3.anode, R6.Pin_0
  N15: LED4.anode, R8.Pin_0
